// Logisim project Alu_32bit.circ as structural Verilog: 1 circuit, main circuit main
module main (
  input  [31:0] A,
  input  [31:0] B,
  input  [4:0] in_3,
  output [31:0] out_4
);

  wire comparator_1_lt, comparator_2_lt;
  wire [31:0] adder_1_out, and_1_out, bit_extender_1_out, bit_extender_2_out, or_1_out, shifter_1_out,
       shifter_2_out, shifter_3_out, subtractor_1_out, xor_1_out;

  Adder #(.width(32)) adder_1 (.a(A), .b(B), .out(adder_1_out));  // open: cin, cout
  Shifter #(.width(32)) shifter_1 (.in(A), .\dist (B[4:0]), .out(shifter_1_out));
  Comparator #(.width(32)) comparator_1 (.a(B), .b(A), .lt(comparator_1_lt));  // open: gt, eq
  Comparator #(.mode("unsigned"), .width(32)) comparator_2 (.a(B), .b(A), .lt(comparator_2_lt));  // open: gt, eq
  assign xor_1_out = B ^ A;  // XOR_Gate xor_1, 32 bits wide
  assign bit_extender_1_out = {{31{comparator_2_lt}}, comparator_2_lt};  // Bit_Extender bit_extender_1
  Shifter #(.shift("lr"), .width(32)) shifter_2 (.in(B), .\dist (A[4:0]), .out(shifter_2_out));
  assign or_1_out = B | A;  // OR_Gate or_1, 32 bits wide
  assign and_1_out = B & A;  // AND_Gate and_1, 32 bits wide
  Subtractor #(.width(32)) subtractor_1 (.a(B), .b(A), .out(subtractor_1_out));  // open: bin, bout
  Shifter #(.shift("ar"), .width(32)) shifter_3 (.in(B), .\dist (A[4:0]), .out(shifter_3_out));
  assign bit_extender_2_out = {{31{comparator_1_lt}}, comparator_1_lt};  // Bit_Extender bit_extender_2
  Multiplexer #(.select(5), .width(32)) multiplexer_1 (
    .in0(adder_1_out), .in1(shifter_1_out), .in2(bit_extender_2_out), .in3(bit_extender_1_out),
    .in4(xor_1_out), .in5(shifter_2_out), .in6(or_1_out), .in7(and_1_out), .in8(subtractor_1_out),
    .in13(shifter_3_out), .out(out_4), .sel(in_3));  // open: in9, in10, in11, in12, in14, in15, in16, in17, in18, in19, in20, in21, in22, in23, in24, in25, in26, in27, in28, in29, in30, in31

  // Notes on the sheet:
  //   add
  //   sll
  //   slt
  //   sltu
  //   xxor
  //   srl
  //   or
  //   and
  //   sra
  //   sub
endmodule
