// Logisim project immediate_generator32bit.circ as structural Verilog: 1 circuit, main circuit main
module main (
  input  [31:0] Instruc,
  output [31:0] I,
  output [31:0] S,
  output [31:0] SB,
  output [31:0] U,
  output [31:0] UJ
);

  wire [31:0] bit_extender_1_out;

  assign bit_extender_1_out = {{12{Instruc[31]}}, Instruc[31:12]};  // Bit_Extender bit_extender_1
  assign I = {{20{Instruc[31]}}, Instruc[31:20]};  // Bit_Extender bit_extender_2
  assign S = {{20{Instruc[31]}}, {Instruc[31:25], Instruc[11:7]}};  // Bit_Extender bit_extender_3
  assign SB = {{19{Instruc[31]}}, {Instruc[31], Instruc[7], Instruc[30:25], Instruc[11:8], 1'b0}};  // Bit_Extender bit_extender_4
  Shifter #(.width(32)) shifter_1 (.in(bit_extender_1_out), .\dist (5'b01100), .out(U));
  assign UJ = {{11{Instruc[31]}}, {Instruc[31], Instruc[19:12], Instruc[20], Instruc[30:21], 1'b0}};  // Bit_Extender bit_extender_5
endmodule
