// Logisim project merl.circ as structural Verilog: 8 circuits, main circuit main
module main (
  input  A,
  input  B,
  output SUM,
  output CARRY
);

  xor xor_1 (SUM, A, B);
  and and_1 (CARRY, A, B);
endmodule

module FULL_ADDER (
  input  A,
  input  B,
  input  Cin,
  output SUM,
  output Cout
);

  wire and_1_out, and_2_out, xor_1_out;

  xor xor_1 (xor_1_out, A, B);
  and and_1 (and_1_out, xor_1_out, Cin);
  and and_2 (and_2_out, B, A);
  xor xor_2 (SUM, xor_1_out, Cin);
  or or_1 (Cout, and_1_out, and_2_out);
endmodule

module bit_4_adder (
  input  [3:0] A,
  input  Cin,
  input  [3:0] B,
  output [3:0] SUM,
  output Cout
);

  wire full_adder_1_cout, full_adder_2_cout, full_adder_3_cout;

  FULL_ADDER full_adder_1 (.A(A[0]), .B(B[0]), .Cin(Cin), .SUM(SUM[0]), .Cout(full_adder_1_cout));
  FULL_ADDER full_adder_2 (.A(A[1]), .B(B[1]), .Cin(full_adder_1_cout), .SUM(SUM[1]), .Cout(full_adder_2_cout));
  FULL_ADDER full_adder_3 (.A(A[2]), .B(B[2]), .Cin(full_adder_2_cout), .SUM(SUM[2]), .Cout(full_adder_3_cout));
  FULL_ADDER full_adder_4 (.A(A[3]), .B(B[3]), .Cin(full_adder_3_cout), .SUM(SUM[3]), .Cout(Cout));
endmodule

module bit_16_adder (
  input  Cin,
  input  [15:0] A,
  input  [15:0] B,
  output [15:0] SUM,
  output Cout
);

  wire bit_4_adder_1_cout, bit_4_adder_2_cout, bit_4_adder_3_cout;

  bit_4_adder bit_4_adder_1 (.A(A[3:0]), .Cin(Cin), .B(B[3:0]), .SUM(SUM[3:0]), .Cout(bit_4_adder_1_cout));
  bit_4_adder bit_4_adder_2 (
    .A(A[7:4]), .Cin(bit_4_adder_1_cout), .B(B[7:4]), .SUM(SUM[7:4]), .Cout(bit_4_adder_2_cout));
  bit_4_adder bit_4_adder_3 (
    .A(A[11:8]), .Cin(bit_4_adder_2_cout), .B(B[11:8]), .SUM(SUM[11:8]), .Cout(bit_4_adder_3_cout));
  bit_4_adder bit_4_adder_4 (.A(A[15:12]), .Cin(bit_4_adder_3_cout), .B(B[15:12]), .SUM(SUM[15:12]), .Cout(Cout));
endmodule

module bit_32_adder (
  input  [31:0] A,
  input  Cin,
  input  [31:0] B,
  output [31:0] SUM,
  output Cout
);

  wire bit_16_adder_1_cout;

  bit_16_adder bit_16_adder_1 (.Cin(Cin), .A(A[15:0]), .B(B[15:0]), .SUM(SUM[15:0]), .Cout(bit_16_adder_1_cout));
  bit_16_adder bit_16_adder_2 (.Cin(bit_16_adder_1_cout), .A(A[31:16]), .B(B[31:16]), .SUM(SUM[31:16]), .Cout(Cout));
endmodule

module R2_1W_32bit_addition (
  input  Cin,
  input  [31:0] A,
  input  [31:0] B,
  output Cout,
  output [31:0] SUM
);

  bit_32_adder bit_32_adder_1 (.A(A), .Cin(Cin), .B(B), .SUM(SUM), .Cout(Cout));
endmodule

module subtracter_with_additor (
  input  in_1,
  input  [31:0] A,
  input  [31:0] B,
  output Cout,
  output [31:0] SUM
);

  wire [31:0] not_1_out;

  assign not_1_out = ~B;  // NOT_Gate not_1, 32 bits wide
  R2_1W_32bit_addition r2_1w_32bit_addition_1 (.Cin(in_1), .A(A), .B(not_1_out), .Cout(Cout), .SUM(SUM));
endmodule

module Multplicator_4bit_2num (
  input  in_1,
  input  in_2,
  input  in_3,
  input  in_4,
  input  in_5,
  input  in_6,
  input  in_7,
  input  in_8,
  input  in_9,
  input  in_10,
  input  in_11,
  input  in_12,
  input  in_13,
  input  in_14,
  input  in_15,
  input  in_16,
  input  in_17,
  input  in_18,
  input  in_19,
  input  in_20,
  input  in_21,
  input  in_22,
  input  in_23,
  input  in_24,
  output [7:0] out_25
);

  wire and_1_out, and_2_out, and_3_out, and_4_out, and_5_out, and_6_out, and_7_out, and_8_out, and_9_out,
       and_10_out, and_11_out, and_12_out, and_13_out, and_14_out, and_15_out, full_adder_2_cout,
       full_adder_2_sum, full_adder_3_cout, full_adder_4_cout, full_adder_4_sum, full_adder_5_cout,
       full_adder_5_sum, full_adder_6_cout, full_adder_7_sum, full_adder_8_cout, full_adder_8_sum,
       full_adder_9_cout, full_adder_10_cout, full_adder_10_sum, full_adder_11_cout, full_adder_12_cout;

  and and_1 (and_1_out, in_19, in_23);
  FULL_ADDER full_adder_1 (
    .A(full_adder_2_cout), .B(and_1_out), .Cin(full_adder_3_cout), .SUM(out_25[6]), .Cout(out_25[7]));
  and and_2 (and_2_out, in_13, in_17);
  FULL_ADDER full_adder_2 (
    .A(full_adder_4_cout), .B(and_2_out), .Cin(full_adder_5_cout), .SUM(full_adder_2_sum),
    .Cout(full_adder_2_cout));
  and and_3 (and_3_out, in_20, in_23);
  FULL_ADDER full_adder_3 (
    .A(full_adder_2_sum), .B(and_3_out), .Cin(full_adder_6_cout), .SUM(out_25[5]), .Cout(full_adder_3_cout));
  and and_4 (and_4_out, in_6, in_10);
  FULL_ADDER full_adder_4 (.A(in_11), .B(and_4_out), .SUM(full_adder_4_sum), .Cout(full_adder_4_cout));  // open: Cin
  and and_5 (and_5_out, in_14, in_17);
  FULL_ADDER full_adder_5 (
    .A(full_adder_4_sum), .B(and_5_out), .Cin(full_adder_8_cout), .SUM(full_adder_5_sum),
    .Cout(full_adder_5_cout));
  and and_6 (and_6_out, in_21, in_23);
  FULL_ADDER full_adder_6 (
    .A(full_adder_5_sum), .B(and_6_out), .Cin(full_adder_9_cout), .SUM(out_25[4]), .Cout(full_adder_6_cout));
  and and_7 (and_7_out, in_1, in_5);
  and and_8 (and_8_out, in_7, in_10);
  FULL_ADDER full_adder_7 (
    .A(and_7_out), .B(and_8_out), .Cin(full_adder_10_cout), .SUM(full_adder_7_sum));  // open: Cout
  and and_9 (and_9_out, in_15, in_17);
  FULL_ADDER full_adder_8 (
    .A(full_adder_7_sum), .B(and_9_out), .Cin(full_adder_11_cout), .SUM(full_adder_8_sum),
    .Cout(full_adder_8_cout));
  and and_10 (and_10_out, in_22, in_23);
  FULL_ADDER full_adder_9 (
    .A(full_adder_8_sum), .B(and_10_out), .Cin(in_24), .SUM(out_25[3]), .Cout(full_adder_9_cout));
  and and_11 (and_11_out, in_8, in_10);
  FULL_ADDER full_adder_10 (
    .A(and_13_out), .B(and_11_out), .Cin(full_adder_12_cout), .SUM(full_adder_10_sum),
    .Cout(full_adder_10_cout));
  and and_12 (and_12_out, in_16, in_17);
  FULL_ADDER full_adder_11 (
    .A(full_adder_10_sum), .B(and_12_out), .Cin(in_18), .SUM(out_25[2]), .Cout(full_adder_11_cout));
  and and_13 (and_13_out, in_2, in_5);
  and and_14 (and_14_out, in_3, in_5);
  and and_15 (and_15_out, in_9, in_10);
  FULL_ADDER full_adder_12 (.A(and_14_out), .B(and_15_out), .Cin(in_12), .SUM(out_25[1]), .Cout(full_adder_12_cout));
  and and_16 (out_25[0], in_4, in_5);
endmodule
