// Logisim project program_counter.circ as structural Verilog: 1 circuit, main circuit main
module main (
  input  [31:0] imm,
  input  sel,
  input  in_3,
  output [31:0] PC_current
);

  wire clock_1_out;
  wire [31:0] adder_1_out, adder_2_out, multiplexer_1_out;

  Register #(.width(32)) register_1 (.D(multiplexer_1_out), .en(1'b1), .clk(clock_1_out), .Q(PC_current), .clr(in_3));
  Clock clock_1 (.out(clock_1_out));
  Adder #(.width(32)) adder_1 (.a(PC_current), .b(32'h4), .out(adder_1_out));  // open: cin, cout
  Adder #(.width(32)) adder_2 (.a(PC_current), .b(imm), .out(adder_2_out));  // open: cin, cout
  Multiplexer #(.width(32)) multiplexer_1 (.in0(adder_1_out), .in1(adder_2_out), .out(multiplexer_1_out), .sel(sel));

  // Notes on the sheet:
  //   Register
  //   pc + 4
  //   DAY 3
  //   PROGRAM GENERATOR
  //   pc + imm
endmodule
